// Logisim project PRojecttttloggi.circ as structural Verilog
module main (
  input  P1,
  input  P2
);

  wire and_1_out, and_2_out, and_3_out, and_4_out, and_5_out, and_6_out, clock_1_out, combat_1_end1,
       combat_1_end2, combat_1_myd1, combat_1_myd2, confirm_out, d_ff_1_q, d_ff_2_q, d_ff_3_q,
       dipswitch_1_p2, dipswitch_2_p2, e0_out, led_decoder_1_l1, led_decoder_1_l2, led_decoder_1_l3,
       led_decoder_1_l4, led_decoder_1_l5, led_decoder_2_l1, led_decoder_2_l2, led_decoder_2_l3,
       led_decoder_2_l4, led_decoder_2_l5, my0_out, not_1_out, not_2_out, not_3_out, register_1_q,
       register_2_q, reset_out, state_1_q2, t_ff_1_q;
  wire [2:0] hpnext_1_hp, hpnext_2_hp;

  Button confirm (.out(confirm_out));
  Clock #(.highDuration(4), .lowDuration(4)) clock_1 (.out(clock_1_out));
  D_Flip_Flop d_ff_1 (.D(confirm_out), .clk(clock_1_out), .Q(d_ff_1_q));  // open: Qn, preset, reset
  D_Flip_Flop d_ff_2 (.D(d_ff_1_q), .clk(clock_1_out), .Q(d_ff_2_q));  // open: Qn, preset, reset
  // DipSwitch #(.number(1)) dipswitch_1: pin names not known; wires that end beside it: clock_1_out, dipswitch_1_p2, P1
  // DipSwitch #(.number(1)) dipswitch_2: pin names not known; wires that end beside it: P2, dipswitch_2_p2
  not not_1 (not_1_out, d_ff_2_q);
  Register #(.width(1)) register_1 (
    .D(dipswitch_1_p2), .en(and_1_out), .clk(clock_1_out), .Q(register_1_q));  // open: clr
  Register #(.width(1)) register_2 (
    .D(dipswitch_2_p2), .en(and_1_out), .clk(clock_1_out), .Q(register_2_q));  // open: clr
  and and_1 (and_1_out, d_ff_1_q, not_1_out);
  LED_part led_1 (.in(and_1_out));
  Button reset (.out(reset_out));
  T_Flip_Flop t_ff_1 (.T(d_ff_3_q), .clk(clock_1_out), .Q(t_ff_1_q), .reset(reset_out));  // open: Qn, preset
  combat combat_1 (
    .T(t_ff_1_q), .Xl(register_1_q), .Rl(register_2_q), .myd2(combat_1_myd2), .myd1(combat_1_myd1),
    .end2(combat_1_end2), .end1(combat_1_end1));
  hpnext hpnext_1 (.clk(clock_1_out), .d2(and_4_out), .d1(and_2_out), .ini(reset_out), .hp(hpnext_1_hp));
  // Probe on hpnext_1_hp
  hpnext hpnext_2 (.clk(clock_1_out), .d2(and_3_out), .d1(and_5_out), .ini(reset_out), .hp(hpnext_2_hp));
  and and_2 (and_2_out, combat_1_myd1, d_ff_3_q);
  and and_3 (and_3_out, d_ff_3_q, combat_1_end2);
  nor my0 (my0_out, hpnext_1_hp[0], hpnext_1_hp[1], hpnext_1_hp[2]);
  nor e0 (e0_out, hpnext_2_hp[0], hpnext_2_hp[1], hpnext_2_hp[2]);
  LED_part Myturn (.in(t_ff_1_q));
  not not_2 (not_2_out, t_ff_1_q);
  LED_part EnTurn (.in(not_2_out));
  LED_DECODER led_decoder_1 (
    .Q2(hpnext_1_hp[2]), .Q1(hpnext_1_hp[1]), .Q0(hpnext_1_hp[0]), .L5(led_decoder_1_l5),
    .L4(led_decoder_1_l4), .L3(led_decoder_1_l3), .L2(led_decoder_1_l2), .L1(led_decoder_1_l1));
  LedBar #(.matrixcols(5)) Pl1 (
    .led0(led_decoder_1_l5), .led1(led_decoder_1_l4), .led2(led_decoder_1_l3), .led3(led_decoder_1_l2),
    .led4(led_decoder_1_l1));
  and and_4 (and_4_out, combat_1_myd2, d_ff_3_q);
  and and_5 (and_5_out, d_ff_3_q, combat_1_end1);
  LED_part P1WIN (.in(e0_out));
  LED_part P2WIN (.in(my0_out));
  state state_1 (.mz(my0_out), .ez(e0_out), .T(t_ff_1_q), .Q2(state_1_q2));  // open: Q1, Q0
  not not_3 (not_3_out, state_1_q2);
  and and_6 (and_6_out, not_3_out, and_1_out);
  LedBar #(.matrixcols(5)) PL2 (
    .led0(led_decoder_2_l5), .led1(led_decoder_2_l4), .led2(led_decoder_2_l3), .led3(led_decoder_2_l2),
    .led4(led_decoder_2_l1));
  LED_DECODER led_decoder_2 (
    .Q2(hpnext_2_hp[2]), .Q1(hpnext_2_hp[1]), .Q0(hpnext_2_hp[0]), .L5(led_decoder_2_l5),
    .L4(led_decoder_2_l4), .L3(led_decoder_2_l3), .L2(led_decoder_2_l2), .L1(led_decoder_2_l1));
  D_Flip_Flop d_ff_3 (.D(and_6_out), .clk(clock_1_out), .Q(d_ff_3_q));  // open: Qn, preset, reset

  // Notes on the sheet:
  //   0 atk/ 1 heavy atk
  //   0 def / 1 counter
endmodule

module HP_Minus1 (
  input  h2,
  input  h1,
  input  h0,
  input  d2,
  input  d1,
  output n2,
  output n1,
  output n0
);

  wire and_1_out, and_2_out, and_3_out, and_4_out, and_5_out, and_6_out, and_7_out, and_8_out, and_9_out,
       and_10_out, and_11_out, not_1_out, not_2_out, not_3_out;

  not not_1 (not_1_out, h0);
  not not_2 (not_2_out, d2);
  not not_3 (not_3_out, d1);
  and and_1 (and_1_out, h2, not_2_out, not_3_out);
  or or_1 (n2, and_1_out, and_2_out);
  and and_2 (and_2_out, h2, h0, not_2_out);
  and and_3 (and_3_out, h2, not_1_out, d1);
  and and_4 (and_4_out, h2, d2);
  and and_5 (and_5_out, h1, not_2_out, not_3_out);
  and and_6 (and_6_out, h1, h0, not_2_out);
  and and_7 (and_7_out, h2, not_1_out, d1);
  and and_8 (and_8_out, h0, not_2_out, not_3_out);
  and and_9 (and_9_out, h1, not_1_out, d1);
  and and_10 (and_10_out, h2, h0, not_3_out);
  and and_11 (and_11_out, h1, h0, d2);
  or or_2 (n1, and_3_out, and_4_out, and_5_out, and_6_out);
  or or_3 (n0, and_7_out, and_8_out, and_9_out, and_10_out, and_11_out);
endmodule

module combat (
  input  T,
  input  Xl,
  input  Rl,
  output myd2,
  output myd1,
  output end2,
  output end1
);

  wire and_2_out, and_3_out, and_5_out, and_6_out, not_1_out, not_2_out, not_3_out;

  not not_1 (not_1_out, T);
  not not_2 (not_2_out, Xl);
  not not_3 (not_3_out, Rl);
  and and_1 (myd2, T, Xl, Rl);
  and and_2 (and_2_out, not_1_out, not_2_out, Rl);
  and and_3 (and_3_out, not_1_out, Xl, not_3_out);
  and and_4 (end2, not_1_out, Xl, Rl);
  and and_5 (and_5_out, T, not_2_out, Rl);
  and and_6 (and_6_out, T, Xl, not_3_out);
  or or_1 (myd1, and_2_out, and_3_out);
  or or_2 (end1, and_5_out, and_6_out);
endmodule

module state (
  input  mz,
  input  ez,
  input  T,
  output Q2,
  output Q1,
  output Q0
);

  wire and_1_out, and_2_out, and_3_out, not_1_out;

  not not_1 (not_1_out, ez);
  and and_1 (and_1_out, ez, T);
  and and_2 (and_2_out, not_1_out, T);
  and and_3 (and_3_out, mz, not_1_out);
  or or_1 (Q2, and_1_out, mz);
  or or_2 (Q0, and_2_out, and_3_out);

  assign Q1 = 1'b0;
endmodule

module LED_DECODER (
  input  Q2,
  input  Q1,
  input  Q0,
  output L5,
  output L4,
  output L3,
  output L2,
  output L1
);

  wire and_2_out;

  and and_1 (L5, Q2, Q0);
  and and_2 (and_2_out, Q1, Q0);
  or or_1 (L2, Q1, Q2);
  or or_2 (L1, Q0, Q1, Q2);
  or or_3 (L3, and_2_out, Q2);

  assign L4 = Q2;
endmodule

module LED (
  input  Q2,
  input  Q1,
  input  Q0,
  output L5,
  output L4,
  output L3,
  output L2,
  output L1
);

  wire and_1_out, and_2_out, and_3_out;

  and and_1 (and_1_out, Q2, Q0);
  and and_2 (and_2_out, Q2, Q1);
  and and_3 (and_3_out, Q1, Q0);
  or or_1 (L2, Q1, Q2);
  or or_2 (L1, Q0, Q1, Q2);
  or or_3 (L5, and_1_out, and_2_out);
  or or_4 (L3, and_3_out, Q2);

  assign L4 = Q2;
endmodule

module hpnext (
  input  clk,
  input  d2,
  input  d1,
  input  ini,
  output [2:0] hp
);

  wire [2:0] hp_minus1_1_n0, multiplexer_1_out;

  Register #(.width(3)) register_1 (.D(multiplexer_1_out), .clk(clk), .Q(hp));  // open: en, clr
  HP_Minus1 hp_minus1_1 (
    .h2(hp[2]), .h1(hp[1]), .h0(hp[0]), .d2(d2), .d1(d1), .n2(hp_minus1_1_n0[2]), .n1(hp_minus1_1_n0[1]),
    .n0(hp_minus1_1_n0[0]));
  Multiplexer #(.width(3)) multiplexer_1 (.in0(hp_minus1_1_n0), .in1(3'b101), .out(multiplexer_1_out), .sel(ini));
endmodule
